// Logisim project drawing.circ as structural Verilog: 3 circuits, main circuit main
module main (
);

  wire [31:0] source_1_data_out, source_data_reg_q;

  Register #(.width(32)) source_data_reg (.D(source_1_data_out), .Q(source_data_reg_q));  // open: en, clk, clr
  source source_1 (.data_out(source_1_data_out));  // open: clk, rst, rd_en
  eth_ip eth_ip_1 (.ff_tx_data(source_data_reg_q));  // open: ff_tx_clk, ff_tx_sop, ff_tx_eop, ff_tx_wren, ff_tx_rdy
endmodule

module eth_ip (
  input  ff_tx_clk,
  input  [31:0] ff_tx_data,
  input  ff_tx_sop,
  input  ff_tx_eop,
  input  ff_tx_wren,
  output ff_tx_rdy
);
endmodule

module source (
  input  clk,
  input  rst,
  input  rd_en,
  output [31:0] data_out
);
endmodule
